# Fritzing sketch Diagrama_interrupiones (saved by Fritzing 0.9.3b)
breadboards: 1

parts:
  Part1 = Arduino Uno (Rev3)
  R1 = Resistor [tolerance=±5% resistance=220 package=THT]
  R2 = Resistor [tolerance=±5% resistance=220 package=THT]
  R3 = Resistor [tolerance=±5% resistance=220 package=THT]
  LED1 = LED - 3mm [color="Red (633nm)" package="3 mm [THT]"]
  LED2 = LED - 3mm [color="Yellow (595nm)" package="3 mm [THT]"]
  LED3 = LED - 3mm [color="Green (560nm)" package="3 mm [THT]"]
  S1 = Pushbutton [package="[THT]"]

nets:
  N1: Part1.D2, S1.Pin_1, S1.Pin_2
  N2: Part1.D3_PWM, R3.Pin_0
  N3: Part1.D4, R1.Pin_0
  N4: Part1.D5_PWM, R2.Pin_0
  N5: Part1.GND, LED1.cathode, LED2.cathode, LED3.cathode
  N6: R1.Pin_1, LED2.anode
  N7: R2.Pin_1, LED3.anode
  N8: R3.Pin_1, LED1.anode
  N9: S1.Pin_3, S1.Pin_4
